// Logisim project byteknight.circ as structural Verilog: 1 circuit, main circuit CPU
module CPU (
  input  [15:0] Const
);

  wire and_1_out, and_2_out, and_3_out, and_4_out, clock_1_out, decoder_1_out0, decoder_1_out1,
       decoder_1_out2, decoder_1_out3, not_1_out;
  wire [1:0] adder_3_out, bit_extender_2_out, multiplexer_1_out;
  wire [15:0] adder_1_out, adder_2_out, bit_extender_1_out, bit_extender_3_out, InstructionMemory_data,
       multiplexer_2_out, multiplexer_3_out, multiplexer_4_out, multiplexer_5_out, multiplexer_6_out,
       multiplier_1_out, PC_q, ram_1_dout, subtractor_1_out, X0_q, X1_q, X2_q, X3_q;

  Clock clock_1 (.out(clock_1_out));
  Register #(.width(16)) PC (.D(adder_1_out), .en(1'b1), .clk(clock_1_out), .Q(PC_q));  // open: clr
  Adder #(.width(16)) adder_1 (.a(Const), .b(PC_q), .out(adder_1_out));  // open: cin, cout
  ROM #(.addrWidth(16), .dataWidth(16)) InstructionMemory (.addr(PC_q), .data(InstructionMemory_data));
  Hex_Digit_Display hex_digit_display_1 (.value(InstructionMemory_data[15:12]));  // open: dp
  Hex_Digit_Display hex_digit_display_2 (.value(InstructionMemory_data[11:8]));  // open: dp
  Hex_Digit_Display hex_digit_display_3 (.value(InstructionMemory_data[3:0]));  // open: dp
  Hex_Digit_Display hex_digit_display_4 (.value(InstructionMemory_data[7:4]));  // open: dp
  Decoder #(.select(2)) decoder_1 (
    .out0(decoder_1_out0), .out1(decoder_1_out1), .out2(decoder_1_out2), .out3(decoder_1_out3),
    .sel(InstructionMemory_data[1:0]));  // open: en
  Multiplexer #(.width(2)) multiplexer_1 (
    .in0(InstructionMemory_data[1:0]), .in1(InstructionMemory_data[5:4]), .out(multiplexer_1_out),
    .sel(InstructionMemory_data[12]));
  and and_1 (and_1_out, decoder_1_out0, InstructionMemory_data[15]);
  and and_2 (and_2_out, decoder_1_out1, InstructionMemory_data[15]);
  and and_3 (and_3_out, decoder_1_out2, InstructionMemory_data[15]);
  and and_4 (and_4_out, decoder_1_out3, InstructionMemory_data[15]);
  Register #(.width(16)) X0 (.D(multiplexer_6_out), .en(and_1_out), .clk(clock_1_out), .Q(X0_q));  // open: clr
  Register #(.width(16)) X1 (.D(multiplexer_6_out), .en(and_2_out), .clk(clock_1_out), .Q(X1_q));  // open: clr
  Register #(.width(16)) X2 (.D(multiplexer_6_out), .en(and_3_out), .clk(clock_1_out), .Q(X2_q));  // open: clr
  Register #(.width(16)) X3 (.D(multiplexer_6_out), .en(and_4_out), .clk(clock_1_out), .Q(X3_q));  // open: clr
  Multiplexer #(.select(2), .width(16)) multiplexer_2 (
    .in0(X0_q), .in1(X1_q), .in2(X2_q), .in3(X3_q), .out(multiplexer_2_out), .sel(InstructionMemory_data[3:2]));
  Multiplexer #(.select(2), .width(16)) multiplexer_3 (
    .in0(X0_q), .in1(X1_q), .in2(X2_q), .in3(X3_q), .out(multiplexer_3_out), .sel(multiplexer_1_out));
  assign bit_extender_1_out = {{14{1'b0}}, InstructionMemory_data[5:4]};  // Bit_Extender bit_extender_1
  Multiplexer #(.width(16)) multiplexer_4 (
    .in0(multiplexer_3_out), .in1(bit_extender_1_out), .out(multiplexer_4_out), .sel(not_1_out));
  not not_1 (not_1_out, InstructionMemory_data[14]);
  LED led_1 (.in(clock_1_out));
  LED led_2 (.in(clock_1_out));
  LED led_3 (.in(clock_1_out));
  LED led_4 (.in(clock_1_out));
  Bit_Extender #(.in_width(16), .out_width(2), .\type ("zero")) bit_extender_2 (
    .in(multiplexer_2_out), .out(bit_extender_2_out));
  LED led_5 (.in(clock_1_out));
  LED led_6 (.in(clock_1_out));
  LED led_7 (.in(clock_1_out));
  LED led_8 (.in(clock_1_out));
  LED led_9 (.in(clock_1_out));
  LED led_10 (.in(clock_1_out));
  LED led_11 (.in(clock_1_out));
  LED led_12 (.in(clock_1_out));
  LED led_13 (.in(clock_1_out));
  LED led_14 (.in(clock_1_out));
  LED led_15 (.in(clock_1_out));
  LED led_16 (.in(clock_1_out));
  LED led_17 (.in(clock_1_out));
  LED led_18 (.in(clock_1_out));
  LED led_19 (.in(clock_1_out));
  LED led_20 (.in(clock_1_out));
  LED led_21 (.in(clock_1_out));
  LED led_22 (.in(clock_1_out));
  LED led_23 (.in(clock_1_out));
  LED led_24 (.in(clock_1_out));
  LED led_25 (.in(clock_1_out));
  LED led_26 (.in(clock_1_out));
  LED led_27 (.in(clock_1_out));
  Adder #(.width(16)) adder_2 (.a(multiplexer_2_out), .b(multiplexer_4_out), .out(adder_2_out));  // open: cin, cout
  Subtractor #(.width(16)) subtractor_1 (
    .a(multiplexer_2_out), .b(multiplexer_4_out), .out(subtractor_1_out));  // open: bin, bout
  Multiplier #(.width(16)) multiplier_1 (
    .a(multiplexer_2_out), .b(multiplexer_4_out), .out(multiplier_1_out));  // open: cin, cout
  Adder #(.width(2)) adder_3 (
    .a(bit_extender_2_out), .b(InstructionMemory_data[5:4]), .out(adder_3_out));  // open: cin, cout
  LED led_28 (.in(clock_1_out));
  LED led_29 (.in(clock_1_out));
  LED led_30 (.in(clock_1_out));
  LED led_31 (.in(clock_1_out));
  LED led_32 (.in(clock_1_out));
  LED led_33 (.in(clock_1_out));
  LED led_34 (.in(clock_1_out));
  LED led_35 (.in(clock_1_out));
  LED led_36 (.in(clock_1_out));
  LED led_37 (.in(clock_1_out));
  LED led_38 (.in(clock_1_out));
  LED led_39 (.in(clock_1_out));
  LED led_40 (.in(clock_1_out));
  LED led_41 (.in(clock_1_out));
  LED led_42 (.in(clock_1_out));
  LED led_43 (.in(clock_1_out));
  LED led_44 (.in(clock_1_out));
  LED led_45 (.in(clock_1_out));
  LED led_46 (.in(clock_1_out));
  LED led_47 (.in(clock_1_out));
  assign bit_extender_3_out = {{14{1'b0}}, adder_3_out};  // Bit_Extender bit_extender_3
  LED led_48 (.in(clock_1_out));
  LED led_49 (.in(clock_1_out));
  LED led_50 (.in(clock_1_out));
  LED led_51 (.in(clock_1_out));
  LED led_52 (.in(clock_1_out));
  LED led_53 (.in(clock_1_out));
  LED led_54 (.in(clock_1_out));
  LED led_55 (.in(clock_1_out));
  LED led_56 (.in(clock_1_out));
  LED led_57 (.in(clock_1_out));
  Multiplexer #(.select(4), .width(16)) multiplexer_5 (
    .in0(adder_2_out), .in1(subtractor_1_out), .in2(multiplier_1_out), .out(multiplexer_5_out),
    .sel(InstructionMemory_data[9:6]));  // open: in3, in4, in5, in6, in7, in8, in9, in10, in11, in12, in13, in14, in15
  RAM #(.addrWidth(16), .asyncread("true"), .dataWidth(16)) ram_1 (
    .addr(bit_extender_3_out), .we(InstructionMemory_data[13]), .oe(1'b1), .clk(clock_1_out),
    .din(multiplexer_3_out), .dout(ram_1_dout));
  Multiplexer #(.width(16)) multiplexer_6 (
    .in0(multiplexer_5_out), .in1(ram_1_dout), .out(multiplexer_6_out), .sel(InstructionMemory_data[10]));

  // Notes on the sheet:
  //   Const: initial=0x1
  //   contents of InstructionMemory (hex, n*v repeats v):
  //   901f d024 9075 d046 908f d0a7 2413 c406
  //   Instruction Memory
  //   Vinayak Ranjan & Sandya Devanahally
  //   I pledge my honor that I have abided by the Stevens Honor System.
endmodule
